# Fritzing sketch Walk through thermal scanner (saved by Fritzing 0.8.7b)

parts:
  Part1 = Arduino Mega 2560 (Rev3)
  U1 = MLX90614 [package=to-39]
  Part2 = SRF05 Ultrasonic Rangefinder
  U3 = M10X2 [package=2x10_lock]
  J1 = Piezo Speaker
  KY-1 = Keyes Relay [package=THT]
  KY-2 = Keyes Relay [package=THT]

nets:
  N1: Part1.A0, U3.9
  N2: Part1.A1, U3.10
  N3: Part1.A2, U3.11
  N4: Part1.A3, U3.12
  N5: Part1.D21/SCL, U1.SCL_VZ
  N6: Part1.D20/SDA, U1.PWM_SDA
  GND: Part1.GND, U1.VSS, U3.16, J1.pin1
  N7: Part1.D11_PWM, U3.14
  N8: Part1.D10_PWM, U3.13
  N9: Part1.D9_PWM, U3.15
  N10: Part1.D8_PWM, J1.pin2
  N11: Part1.D2_PWM, Part2.Echo
  N12: Part1.D3_PWM, Part2.Trig
  N13: Part1.D5_PWM, KY-1.signal
  N14: Part1.D6_PWM, KY-2.signal
  5V: Part1.5V, U1.VDD, Part2.VCC
  N15: Part1.D24, U3.1
  N16: Part1.D25, U3.2
  N17: Part1.D26, U3.3
  N18: Part1.D27, U3.5
  N19: Part1.D28, U3.6
  N20: Part1.D29, U3.7
  N21: U3.4, U3.8

notes:
  Ultrasonic sensor
  HC-SR04
  Buzzer

custom parts:
  Keyes Relay: The Keyes 5V relay module is suitable for SCM development, home appliance control. It uses a 5V~12V TIL control signal which can control DC / AC signal.
